# Fritzing sketch en_son_devre (saved by Fritzing 1.0.2b)
breadboards: 2

parts:
  Parça1 = Arduino Mega 2560 (Rev3)
  U1 = 74HC595 [package="DIP16 [THT]"]
  U2 = 74HC595 [package="DIP16 [THT]"]
  U3 = ESP32-38PinWide [part_number=ESP32-38PinWide]
  LED1 = smd LED [color="Red (633nm)" package="1206 [SMD]"]
  LED2 = smd LED [color="Green (565nm)" package="1206 [SMD]"]
  LED3 = smd LED [color="Green (565nm)" package="1206 [SMD]"]
  LED4 = smd LED [color="Red (633nm)" package="1206 [SMD]"]
  LED5 = smd LED [color="Red (633nm)" package="1206 [SMD]"]
  LED6 = smd LED [color="Green (565nm)" package="1206 [SMD]"]
  LED8 = smd LED [color="Green (565nm)" package="1206 [SMD]"]
  LED9 = smd LED [color="Red (633nm)" package="1206 [SMD]"]
  LED10 = smd LED [color="Green (565nm)" package="1206 [SMD]"]
  LED11 = smd LED [color="Red (633nm)" package="1206 [SMD]"]
  LED12 = smd LED [color="Green (565nm)" package="1206 [SMD]"]
  LED13 = smd LED [color="Red (633nm)" package="1206 [SMD]"]
  LED14 = smd LED [color="Green (565nm)" package="1206 [SMD]"]
  LED16 = smd LED [color="Red (633nm)" package="1206 [SMD]"]
  LED18 = smd LED [color="Green (565nm)" package="1206 [SMD]"]
  LED19 = smd LED [color="Red (633nm)" package="1206 [SMD]"]
  LED20 = smd LED [color="Green (565nm)" package="1206 [SMD]"]
  M1 = BME280
  Water_Level_Sensor1 = Water Level Sensor
  S1 = H-Bridge with L298N
  A1 = lcd color display 1.3in 240x240 7pin interface [package=THT]
  DS1 = DS18B20 1-Wire Temperature Sensor Probe
  WATER_PUMP1 = water pump/motor
  Parça2 = MQ-4
  Parça3 = MQ-4
  Mod1 = KY-018 Photoresistor Module [package="Breakout board"]
  R2 = Resistor [tolerance=±5% resistance=220 package="2010 [SMD]"]
  R3 = Resistor [tolerance=±5% resistance=220 package="2010 [SMD]"]
  R4 = Resistor [tolerance=±5% resistance=220 package="2010 [SMD]"]
  R5 = Resistor [tolerance=±5% resistance=220 package="2010 [SMD]"]
  S2 = Pushbutton [package="[SMD]"]
  S3 = Pushbutton [package="[SMD]"]
  R6 = Resistor [tolerance=±5% resistance=220 package="2010 [SMD]"]
  R7 = Resistor [tolerance=±5% resistance=220 package="2010 [SMD]"]
  R8 = Resistor [tolerance=±5% resistance=220 package="2010 [SMD]"]
  M2 = Stepper Motor - Bipolar
  BAT1 = BC9VPC [package=bc9vpc]

nets:
  N1: Parça1.A12, Mod1.S
  N2: Parça1.A13, Parça2.AO
  N3: Parça1.A14, Parça3.AO
  N4: Parça1.A15, Water_Level_Sensor1.SIG
  N5: Parça1.D21/SCL, Parça1.SCL, M1.SCL, R2.Pin_0
  N6: Parça1.D20/SDA, Parça1.SDA, M1.SDA, R3.Pin_0
  N7: Parça1.D9_PWM, S1.ENB
  N8: Parça1.D8_PWM, S1.ENA
  3V3: Parça1.3V3, M1.VIN
  VCC: Parça1.5V, Parça1.D2_PWM, Parça1.D3_PWM, U1.MR, U1.VCC, U2.MR, U2.VCC, U3.VIN, Water_Level_Sensor1.VCC, DS1.VDD, Parça2.VCC, Parça3.VCC, Mod1.Vin, Mod1.-, S2.Pin_3, S2.Pin_4, S3.Pin_3, S3.Pin_4
  GND: Parça1.GND, U1.GND, U1.OE, U2.OE, U3.GND, LED1.cathode, LED2.cathode, LED3.cathode, LED4.cathode, LED5.cathode, LED6.cathode, LED8.cathode, LED9.cathode, LED10.cathode, LED11.cathode, LED12.cathode, LED13.cathode, LED14.cathode, LED16.cathode, LED18.cathode, LED19.cathode, LED20.cathode, M1.GND, Water_Level_Sensor1.GND, S1.GND, DS1.GND, Parça2.GND, Parça3.GND, R6.Pin_1, R7.Pin_1, BAT1.V-
  N9: Parça1.D0_RX0, U3.GPIO1
  N10: Parça1.D1_TX0, U3.GPIO3
  N11: Parça1.D4_PWM, R4.Pin_0
  N12: Parça1.D5_PWM, R5.Pin_0
  N13: Parça1.D6_PWM, R8.Pin_0
  N14: Parça1.D30, U1.DS
  N15: Parça1.D31, U1.ST_CP, U2.ST_CP
  N16: Parça1.D33, U1.SH_CP, U2.SH_CP
  N17: Parça1.D41, S1.IN4
  N18: Parça1.D43, S1.IN3
  N19: Parça1.D45, S1.IN2
  N20: Parça1.D47, S1.IN1
  N21: Parça1.D53, DS1.DQ
  N22: U1.Q1, LED1.anode
  N23: U1.Q2, LED2.anode
  N24: U1.Q3, LED4.anode
  N25: U1.Q4, LED3.anode
  N26: U1.Q5, LED5.anode
  N27: U1.Q6, LED6.anode
  N28: U1.Q7, LED19.anode
  N29: U1.Q7', U2.DS
  N30: U1.Q0, LED8.anode
  N31: U2.Q1, LED9.anode
  N32: U2.Q2, LED10.anode
  N33: U2.Q3, LED11.anode
  N34: U2.Q4, LED12.anode
  N35: U2.Q5, LED13.anode
  N36: U2.Q6, LED14.anode
  N37: U2.Q7, LED16.anode
  N38: U2.GND, LED18.anode
  N39: U2.Q0, LED20.anode
  N40: S1.12V, BAT1.V+
  N41: S1.M1-01, M2.D
  N42: S1.M1-02, M2.B
  N43: S1.M2-01, WATER_PUMP1.pin_2
  N44: S1.M2-02, WATER_PUMP1.pin_1
  N45: A1.SCL, R2.Pin_1
  N46: A1.SDA, R3.Pin_1
  N47: A1.RES, R4.Pin_1
  N48: A1.DC, R5.Pin_1
  N49: A1.BLK, R8.Pin_1
  N50: S2.Pin_1, S2.Pin_2, R6.Pin_0
  N51: S3.Pin_1, S3.Pin_2, R7.Pin_0

notes:
  ESP32
  WiFi bağlantısı
  Web Server
  Arduino Mega
  ST7735
  OLED ekran
  LDR Modülü
  L298N
  Motor Sürücü Kartı
  BMP280
  Basınç, Nem,
  Sıcaklık Sensörü
  MQ4
  Metan Gazı Sensörü
  MQ135
  Hava Kirliliği Sensörü
  DS18B20
  Su Geçirmez Sıcaklık Sensörü
  Su Seviyesi Sensörü
  Perilstaltik
  Sıvı Pompası
  17HS4401
  Nema 17 Step Motor

custom parts:
  ESP32-38PinWide: Generic 38-Pin ESP32 with wide format (only access to one side of pins on a breadboard) based on Stephen Lilley's HiLetgo ESP-WROOM-32 ESP32 ESP-32S Development Board.
  BME280: Temperature Humidity Barometric presure Sensor
  Water Level Sensor: A water level sensor. This sensor operates at 3V to 5V. The Sig (signal) pin outputs an analogue signal that is in proportion to the amount of water in contact with the sensor.
  H-Bridge with L298N: h-bridge
  lcd color display 1.3in 240x240 7pin interface: 1.3 Inch Color 240 x 240 IPS TFT LCD Display Screen Module Board 7 Pin 4 Wire ST7789VW Drive IC SPI interface.
  water pump/motor: WATER PUMP BY ARDUBLOCKTR
  KY-018 Photoresistor Module: KY-018 Photoresistor module, used to measure light intensity. It can determine the presence or absence of light.
